# Fritzing sketch button_led_test (saved by Fritzing 0.9.3b)
breadboards: 1

parts:
  S1 = Pushbutton [package="[THT]"]
  LED1 = LED - 5mm [color="Yellow (595nm)" package="5 mm [THT]"]
  Raspberry_Pi_1 = Raspberry Pi 3 [part_number=RPI-3-V1.2]
  R1 = Resistor [tolerance=±5% resistance=330 package=THT]

nets (from the breadboard view):
  N1: S1.Pin_1, S1.Pin_2, Raspberry_Pi_1.GIPO21
  N2: S1.Pin_3, S1.Pin_4, Raspberry_Pi_1.3v3
  N3: LED1.cathode, Raspberry_Pi_1.GIPO19
  N4: LED1.anode, R1.Pin_0
  N5: Raspberry_Pi_1.GND, R1.Pin_1
